# Fritzing sketch MainBoard Sketch V2 (saved by Fritzing 0.9.3b)
circuit board: 8.46667cm x 5.64444cm
breadboards: 1

parts:
  1000yF = Capacitor Polarized [package=panasonic_g]
  WeMos_D1_Mini1 = WeMos D1 Mini
  5V = Camdenboss CTB0158-2 [part_number=CTB0158-2 package=THT]
  I2C_SCL/SDA = Header 2 [package=jst-2-pth]
  I2C_VCC/GND = Header 2 [package=jst-2-pth]
  Control_Pad = Header 6 [package=1x06-smd]  # not connected
  Room_Pad = Header 6 [package=1x06-smd]

nets:
  N1: 1000yF.+, WeMos_D1_Mini1.5V, 5V.pin2
  N2: 1000yF.-, WeMos_D1_Mini1.G, 5V.pin1, I2C_VCC/GND.1
  N3: WeMos_D1_Mini1.3V3, I2C_VCC/GND.2
  N4: WeMos_D1_Mini1.D1, I2C_SCL/SDA.1
  N5: WeMos_D1_Mini1.D2, I2C_SCL/SDA.2
  N6: WeMos_D1_Mini1.D3, Room_Pad.2
  N7: WeMos_D1_Mini1.D4, Room_Pad.4

custom parts:
  WeMos D1 Mini: The D1 mini is a mini wifi board based on ESP-8266EX.
