# Fritzing sketch MainBoard Sketch (saved by Fritzing 0.9.3b)
circuit board: 8.46667cm x 5.64444cm
breadboards: 1

parts:
  5V = Camdenboss CTB0158-2 [part_number=CTB0158-2 package=THT]
  1000yF = Capacitor Polarized [package=panasonic_g]
  I2C_SCL/SDA = Header 2 [package=jst-2-pth]
  I2C_VCC/GND = Header 2 [package=jst-2-pth]
  WeMos_D1_Mini1 = WeMos D1 Mini
  Room_Pad = Header 6 [package=1x06-smd]
  Control_Pad = Header 6 [package=1x06-smd]

nets:
  N1: 5V.pin1, 1000yF.-, I2C_VCC/GND.1, WeMos_D1_Mini1.G, Room_Pad.1, Control_Pad.6
  N2: 5V.pin2, 1000yF.+, WeMos_D1_Mini1.5V
  N3: I2C_SCL/SDA.1, WeMos_D1_Mini1.D1
  N4: I2C_SCL/SDA.2, WeMos_D1_Mini1.D2
  N5: I2C_VCC/GND.2, WeMos_D1_Mini1.3V3
  N6: WeMos_D1_Mini1.D3, Room_Pad.5
  N7: WeMos_D1_Mini1.D4, Room_Pad.3
  N8: WeMos_D1_Mini1.D5, Control_Pad.1
  N9: WeMos_D1_Mini1.D6, Control_Pad.2
  N10: WeMos_D1_Mini1.D7, Control_Pad.3

custom parts:
  WeMos D1 Mini: The D1 mini is a mini wifi board based on ESP-8266EX.
